// Logisim project MIC-1.circ as structural Verilog: 25 circuits, main circuit main
module main (
  input  CLK,
  output [31:0] PC,
  output [8:0] MPC,
  output [31:0] B,
  output [31:0] C
);

  wire data_path_1_p8, data_path_1_p9, data_path_1_p10, data_path_1_p11, data_path_1_p12, data_path_1_p13,
       data_path_1_p14, data_path_1_p15, data_path_1_p16, data_path_1_p24, data_path_1_p25, data_path_1_p26,
       data_path_1_p27, data_path_1_p28, data_path_1_p29, data_path_1_p30, data_path_1_p31, data_path_1_p32,
       data_path_1_p34, data_path_1_p35, RESET_out;
  wire [1:0] data_path_1_p21, data_path_1_p38;
  wire [2:0] data_path_1_p7;
  wire [3:0] data_path_1_p17;
  wire [7:0] data_path_1_p33, mem_1_mem_fetch;
  wire [31:0] data_path_1_p1, data_path_1_p2, mem_1_mrm_rd;

  Mem mem_1 (
    .MEM_ADDR_32(data_path_1_p1), .CLK(CLK), .MEM_WR(data_path_1_p2), .MRM_RD(mem_1_mrm_rd),
    .MEM_FETCH(mem_1_mem_fetch), .wr(data_path_1_p7[2]), .rd(data_path_1_p7[1]), .fetch(data_path_1_p7[0]),
    .MEM_ADDR_8(PC));
  Button RESET (.out(RESET_out));
  // Data_Path data_path_1: pin names not known; wires that end beside it: data_path_1_p1, data_path_1_p2, mem_1_mrm_rd, data_path_1_p7[1], PC, mem_1_mem_fetch, data_path_1_p7[0], data_path_1_p8, data_path_1_p9, data_path_1_p10, data_path_1_p11, data_path_1_p12, data_path_1_p13, data_path_1_p14, data_path_1_p15, data_path_1_p16, data_path_1_p17[0], data_path_1_p17[1], data_path_1_p17[2], data_path_1_p17[3], data_path_1_p21, CLK, RESET_out, data_path_1_p24, data_path_1_p25, data_path_1_p26, data_path_1_p27, data_path_1_p28, data_path_1_p29, data_path_1_p30, data_path_1_p31, data_path_1_p32, data_path_1_p33, data_path_1_p34, data_path_1_p35, B, C, data_path_1_p38[0], data_path_1_p38[1]
  Control_Unit control_unit_1 (
    .CLK(CLK), .RESET(RESET_out), .MBR(data_path_1_p33), .N(data_path_1_p34), .Z(data_path_1_p35), .MPC(MPC),
    .MDR_B(data_path_1_p24), .PC_B(data_path_1_p25), .MBR_B(data_path_1_p26), .MBRU_B(data_path_1_p27),
    .SP_B(data_path_1_p28), .LV_B(data_path_1_p29), .CPP_B(data_path_1_p30), .TOS_B(data_path_1_p31),
    .OPC_B(data_path_1_p32), .Mem(data_path_1_p7), .ALU({data_path_1_p21, data_path_1_p17}),
    .Shifter(data_path_1_p38), .H_C(data_path_1_p16), .OPC_C(data_path_1_p15), .TOS_C(data_path_1_p14),
    .CPP_C(data_path_1_p13), .LV_C(data_path_1_p12), .SP_C(data_path_1_p11), .PC_C(data_path_1_p10),
    .MDR_C(data_path_1_p9), .MAR_C(data_path_1_p8));
endmodule

module Mem (
  input  wr,
  input  [31:0] MEM_WR,
  input  [31:0] MEM_ADDR_32,
  input  rd,
  input  [31:0] MEM_ADDR_8,
  input  fetch,
  input  CLK,
  output [31:0] MRM_RD,
  output [7:0] MEM_FETCH
);

  wire not_1_out, not_2_out, not_3_out;
  wire [7:0] ram_2_data;
  wire [31:0] ram_1_data;

  not not_1 (not_1_out, CLK);
  not not_2 (not_2_out, wr);
  RAM #(.addrWidth(24), .dataWidth(32)) ram_1 (
    .addr(MEM_ADDR_32[23:0]), .data(ram_1_data), .sel(1'b1), .clk(not_1_out), .ld(not_2_out), .clr(1'b0));
  assign ram_1_data = wr ? MEM_WR : 32'bz;  // Controlled_Buffer controlled_buffer_1
  assign MRM_RD = rd ? ram_1_data : 32'bz;  // Controlled_Buffer controlled_buffer_2
  not not_3 (not_3_out, CLK);
  assign MEM_FETCH = fetch ? ram_2_data : 8'bz;  // Controlled_Buffer controlled_buffer_3
  RAM #(.addrWidth(24)) ram_2 (
    .addr(MEM_ADDR_8[23:0]), .data(ram_2_data), .sel(1'b1), .clk(not_3_out), .clr(1'b0));  // open: ld

  // Notes on the sheet:
  //   Una truchada porque Logisim no tiene
  //   un bloque de memoria con dos canales de datos
endmodule

module Control_Unit (
  input  CLK,
  input  RESET,
  input  [7:0] MBR,
  input  N,
  input  Z,
  output [8:0] MPC,
  output MDR_B,
  output PC_B,
  output MBR_B,
  output MBRU_B,
  output SP_B,
  output LV_B,
  output CPP_B,
  output TOS_B,
  output OPC_B,
  output [2:0] Mem,
  output [5:0] ALU,
  output [1:0] Shifter,
  output H_C,
  output OPC_C,
  output TOS_C,
  output CPP_C,
  output LV_C,
  output SP_C,
  output PC_C,
  output MDR_C,
  output MAR_C
);

  wire and_1_out, and_2_out, d_flipflop_asc_1_p4, d_flipflop_asc_1_p5, d_flipflop_asc_2_p5;
  wire [2:0] mir_1_jam;
  wire [3:0] control_store_1_cs_s4, mir_1_b;
  wire [7:0] mir_1_addr, multiplexer_3_out, or_2_out;
  wire [8:0] multiplexer_1_out, multiplexer_2_out;
  wire [8:8] mir_1_addr_2, or_1_out;
  wire [31:0] control_store_1_cs_s32;

  Multiplexer #(.width(9), .enable("false")) multiplexer_1 (
    .in0({9{1'b1}}), .in1(9'hff), .out(multiplexer_1_out), .sel(RESET));
  Multiplexer #(.width(9), .enable("false")) multiplexer_2 (
    .in0({9{1'b1}}), .in1(9'h100), .out(multiplexer_2_out), .sel(RESET));
  and and_1 (and_1_out, d_flipflop_asc_1_p5, mir_1_jam[1]);
  // D_FlipFlop_Asc d_flipflop_asc_1: pin names not known; wires that end beside it: N, CLK, 1'b1, d_flipflop_asc_1_p4, d_flipflop_asc_1_p5
  // D_FlipFlop_Asc d_flipflop_asc_2: pin names not known; wires that end beside it: Z, CLK, 1'b1, d_flipflop_asc_1_p4, d_flipflop_asc_2_p5
  Multiplexer #(.width(8), .enable("false")) multiplexer_3 (
    .in0(mir_1_addr), .in1(or_2_out), .out(multiplexer_3_out), .sel(mir_1_jam[2]));
  or or_1 (or_1_out[8], and_1_out, and_2_out, mir_1_addr_2[8]);
  and and_2 (and_2_out, d_flipflop_asc_2_p5, mir_1_jam[0]);
  assign or_2_out = MBR | mir_1_addr;  // OR_Gate or_2, 8 bits wide
  not not_1 (d_flipflop_asc_1_p4, RESET);
  MPC mpc_1 (
    .Entrada({or_1_out[8], multiplexer_3_out}), .CLK(CLK), .Salida(MPC), .nPRE(multiplexer_1_out),
    .nCLR(multiplexer_2_out));
  Control_Store control_store_1 (.CS_E(MPC), .CS_S32(control_store_1_cs_s32), .CS_S4(control_store_1_cs_s4));
  MIR mir_1 (
    .Entrada_4(control_store_1_cs_s4), .Entrada_32(control_store_1_cs_s32), .CLK(CLK), .RESET(RESET),
    .B(mir_1_b), .Mem(Mem), .C({H_C, OPC_C, TOS_C, CPP_C, LV_C, SP_C, PC_C, MDR_C, MAR_C}),
    .ALU({Shifter, ALU}), .JAM(mir_1_jam), .Addr({mir_1_addr_2[8], mir_1_addr}));
  Decoder #(.select(4), .enable("false")) decoder_1 (
    .out0(MDR_B), .out1(PC_B), .out2(MBR_B), .out3(MBRU_B), .out4(SP_B), .out5(LV_B), .out6(CPP_B),
    .out7(TOS_B), .out8(OPC_B), .sel(mir_1_b));  // open: out9, out10, out11, out12, out13, out14, out15
endmodule

module Control_Store (
  input  [8:0] CS_E,
  output [31:0] CS_S32,
  output [3:0] CS_S4
);

  ROM #(.addrWidth(9), .dataWidth(32)) rom_1 (.addr(CS_E), .data(CS_S32), .sel(1'b1));
  ROM #(.addrWidth(9), .dataWidth(4)) rom_2 (.addr(CS_E), .data(CS_S4), .sel(1'b1));

  // Notes on the sheet:
  //   Otra truchada porque Logisim no tiene
  //   un bloque de memoria mas ancho que 32 bits
  //   contents of rom_1 (hex, n*v repeats v):
  //   80000000 255*0 435021
  //   contents of rom_2 (hex, n*v repeats v):
  //   f 255*0 1
endmodule

module MPC (
  input  [8:0] nPRE,
  input  [8:0] Entrada,
  input  CLK,
  input  [8:0] nCLR,
  output [8:0] Salida
);

  // D_Latch d_latch_1: pin names not known; wires that end beside it: Entrada[8], CLK, nPRE[8], nCLR[8], Salida[8]
  // D_Latch d_latch_2: pin names not known; wires that end beside it: Entrada[7], CLK, nPRE[7], nCLR[7], Salida[7]
  // D_Latch d_latch_3: pin names not known; wires that end beside it: Entrada[6], CLK, nPRE[6], nCLR[6], Salida[6]
  // D_Latch d_latch_4: pin names not known; wires that end beside it: Entrada[5], CLK, nPRE[5], nCLR[5], Salida[5]
  // D_Latch d_latch_5: pin names not known; wires that end beside it: Entrada[4], CLK, nPRE[4], nCLR[4], Salida[4]
  // D_Latch d_latch_6: pin names not known; wires that end beside it: Entrada[3], CLK, nPRE[3], nCLR[3], Salida[3]
  // D_Latch d_latch_7: pin names not known; wires that end beside it: Entrada[2], CLK, nPRE[2], nCLR[2], Salida[2]
  // D_Latch d_latch_8: pin names not known; wires that end beside it: Entrada[1], CLK, nPRE[1], nCLR[1], Salida[1]
  // D_Latch d_latch_9: pin names not known; wires that end beside it: Entrada[0], CLK, nPRE[0], nCLR[0], Salida[0]
endmodule

module MIR (
  input  [3:0] Entrada_4,
  input  [31:0] Entrada_32,
  input  CLK,
  input  RESET,
  output [3:0] B,
  output [2:0] Mem,
  output [8:0] C,
  output [7:0] ALU,
  output [2:0] JAM,
  output [8:0] Addr
);

  wire [3:0] multiplexer_2_out, multiplexer_4_out, not_2_out;
  wire [31:0] multiplexer_1_out, multiplexer_3_out, not_1_out;

  Multiplexer #(.width(32), .enable("false")) multiplexer_1 (
    .in0({32{1'b1}}), .in1(not_1_out), .out(multiplexer_1_out), .sel(RESET));
  assign not_1_out = ~32'h435021;  // NOT_Gate not_1, 32 bits wide
  assign not_2_out = ~4'b0001;  // NOT_Gate not_2, 4 bits wide
  Multiplexer #(.width(4), .enable("false")) multiplexer_2 (
    .in0(4'b1111), .in1(not_2_out), .out(multiplexer_2_out), .sel(RESET));
  Multiplexer #(.width(32), .enable("false")) multiplexer_3 (
    .in0({32{1'b1}}), .in1(32'h435021), .out(multiplexer_3_out), .sel(RESET));
  Multiplexer #(.width(4), .enable("false")) multiplexer_4 (
    .in0(4'b1111), .in1(4'b0001), .out(multiplexer_4_out), .sel(RESET));
  Register_32_bits_Des register_32_bits_des_1 (
    .Entrada(Entrada_32), .CLK(CLK), .Salida({Addr, JAM, ALU, C, Mem}), .nPRE(multiplexer_1_out),
    .nCLR(multiplexer_3_out));
  Register_4_bits_Des register_4_bits_des_1 (
    .Entrada(Entrada_4), .CLK(CLK), .Salida(B), .nPRE(multiplexer_2_out), .nCLR(multiplexer_4_out));
endmodule

module Data_Path (
  input  MAR_C,
  input  [31:0] MEM_RD,
  input  MDR_B,
  input  MDR_C,
  input  rd,
  input  [7:0] MEM_FETCH,
  input  PC_B,
  input  PC_C,
  input  MBR,
  input  fetch,
  input  MBRU,
  input  SP_B,
  input  SP_C,
  input  LV_B,
  input  LV_C,
  input  CPP_B,
  input  CPP_C,
  input  RESET,
  input  TOS_B,
  input  TOS_C,
  input  OPC_B,
  input  OPC_C,
  input  H_C,
  input  CLK,
  input  INC,
  input  INVA,
  input  ENA,
  input  ENB,
  input  [1:0] F,
  input  SRA1,
  input  SLL8,
  output [31:0] MEM_MAR,
  output [31:0] MEM_WR,
  output [31:0] MEM_PC,
  output [7:0] OP_CODE,
  output [31:0] B,
  output N,
  output [31:0] out_38
);

  wire [7:0] multiplexer_1_out;
  wire [31:0] multiplexer_2_out, undriven, undriven_2;

  Multiplexer #(.width(8), .enable("false")) multiplexer_1 (
    .in0({8{1'b1}}), .in1({8{1'b0}}), .out(multiplexer_1_out), .sel(RESET));
  Multiplexer #(.width(32), .enable("false")) multiplexer_2 (
    .in0({32{1'b1}}), .in1({32{1'b0}}), .out(multiplexer_2_out), .sel(RESET));
  Multiplexer #(.width(32), .enable("false")) multiplexer_3 (.in0(out_38), .in1(MEM_RD), .sel(rd));  // open: out
  assign B = MDR_B ? MEM_WR : 32'bz;  // Controlled_Buffer controlled_buffer_1
  assign B = PC_B ? MEM_PC : 32'bz;  // Controlled_Buffer controlled_buffer_2
  MBR_EN mbr_en_1 (.in_1(OP_CODE), .Salida_Signada(B), .Salida_No_Signada(B), .MRB(MBR), .MBRU(MBRU));
  Controlled_Buffer #(.width(32)) controlled_buffer_3 (.out(B), .en(SP_B));  // open: in
  Controlled_Buffer #(.width(32)) controlled_buffer_4 (.out(B), .en(LV_B));  // open: in
  Controlled_Buffer #(.width(32)) controlled_buffer_5 (.out(B), .en(CPP_B));  // open: in
  Controlled_Buffer #(.width(32)) controlled_buffer_6 (.out(B), .en(TOS_B));  // open: in
  Controlled_Buffer #(.width(32)) controlled_buffer_7 (.out(B), .en(OPC_B));  // open: in
  Shifter shifter_1 (.Salida(out_38), .Entrada(undriven_2), .SRA1(SRA1), .SLL8(SLL8));
  ALU_32_bit alu_32_bit_1 (
    .INVA(INVA), .A0(undriven[0]), .ENA(ENA), .B0(B[0]), .ENB(ENB), .F0(F[0]), .F1(F[1]), .B1(B[1]),
    .A2(undriven[2]), .B2(B[2]), .A3(undriven[3]), .B3(B[3]), .A4(undriven[4]), .B4(B[4]), .A5(undriven[5]),
    .B5(B[5]), .A6(undriven[6]), .B6(B[6]), .A7(undriven[7]), .B7(B[7]), .A8(undriven[8]), .B8(B[8]),
    .A9(undriven[9]), .B9(B[9]), .A10(undriven[10]), .B10(B[10]), .A11(undriven[11]), .B11(B[11]),
    .A12(undriven[12]), .B12(B[12]), .A13(undriven[13]), .B13(B[13]), .A14(undriven[14]), .B14(B[14]),
    .A15(undriven[15]), .B15(B[15]), .A16(undriven[16]), .B16(B[16]), .A17(undriven[17]), .B17(B[17]),
    .A18(undriven[18]), .B18(B[18]), .A19(undriven[19]), .B19(B[19]), .A20(undriven[20]), .B20(B[20]),
    .A21(undriven[21]), .B21(B[21]), .A22(undriven[22]), .B22(B[22]), .A23(undriven[23]), .B23(B[23]),
    .A24(undriven[24]), .B24(B[24]), .A25(undriven[25]), .B25(B[25]), .A26(undriven[26]), .B26(B[26]),
    .A27(undriven[27]), .B27(B[27]), .A28(undriven[28]), .B28(B[28]), .A29(undriven[29]), .B29(B[29]),
    .A30(undriven[30]), .B30(B[30]), .A31(undriven[31]), .B31(B[31]), .output_18(undriven_2[17]),
    .output_19(undriven_2[18]), .output_20(undriven_2[19]), .output_21(undriven_2[20]),
    .output_22(undriven_2[21]), .output_23(undriven_2[22]), .output_24(undriven_2[23]),
    .output_25(undriven_2[24]), .output_26(undriven_2[25]), .output_27(undriven_2[26]),
    .output_28(undriven_2[27]), .output_29(undriven_2[28]), .output_30(undriven_2[29]),
    .output_31(undriven_2[30]), .output_32(undriven_2[31]), .Carry_Out(N), .Carry_in(INC), .A1(undriven[1]));  // open: output, output_2, output_3, output_4, output_5, output_6, output_7, output_8, output_9, output_10, output_11, output_12, output_13, output_14, output_15, output_16, output_17

  // Notes on the sheet:
  //   Preset 8 Bits
  //   Clear 8 Bits
  //   Preset 32 Bits
  //   Clear 32 Bits
  //   A
  //   B
  //   Bus C
  //   Bus B
endmodule

module Register_32_bits_Hold___Paralel_Load (
  input  [31:0] nPRE,
  input  [31:0] Entrada,
  input  LOAD,
  input  CLK,
  input  [31:0] nCLR,
  output [31:0] Salida
);

  wire [31:0] multiplexer_1_out;

  Multiplexer #(.width(32), .enable("false")) multiplexer_1 (
    .in1(Entrada), .out(multiplexer_1_out), .sel(LOAD));  // open: in0
  D_FlipFlop_Des d_flipflop_des_1 (
    .D(multiplexer_1_out[31]), .CLK(CLK), .Q(Salida[31]), .nPRE(nPRE[31]), .nCLR(nCLR[31]));  // open: nQ
  D_FlipFlop_Des d_flipflop_des_2 (
    .D(multiplexer_1_out[30]), .CLK(CLK), .Q(Salida[30]), .nPRE(nPRE[30]), .nCLR(nCLR[30]));  // open: nQ
  D_FlipFlop_Des d_flipflop_des_3 (
    .D(multiplexer_1_out[29]), .CLK(CLK), .Q(Salida[29]), .nPRE(nPRE[29]), .nCLR(nCLR[29]));  // open: nQ
  D_FlipFlop_Des d_flipflop_des_4 (
    .D(multiplexer_1_out[28]), .CLK(CLK), .Q(Salida[28]), .nPRE(nPRE[28]), .nCLR(nCLR[28]));  // open: nQ
  D_FlipFlop_Des d_flipflop_des_5 (
    .D(multiplexer_1_out[27]), .CLK(CLK), .Q(Salida[27]), .nPRE(nPRE[27]), .nCLR(nCLR[27]));  // open: nQ
  D_FlipFlop_Des d_flipflop_des_6 (
    .D(multiplexer_1_out[26]), .CLK(CLK), .Q(Salida[26]), .nPRE(nPRE[26]), .nCLR(nCLR[26]));  // open: nQ
  D_FlipFlop_Des d_flipflop_des_7 (
    .D(multiplexer_1_out[25]), .CLK(CLK), .Q(Salida[25]), .nPRE(nPRE[25]), .nCLR(nCLR[25]));  // open: nQ
  D_FlipFlop_Des d_flipflop_des_8 (
    .D(multiplexer_1_out[24]), .CLK(CLK), .Q(Salida[24]), .nPRE(nPRE[24]), .nCLR(nCLR[24]));  // open: nQ
  D_FlipFlop_Des d_flipflop_des_9 (
    .D(multiplexer_1_out[23]), .CLK(CLK), .Q(Salida[23]), .nPRE(nPRE[23]), .nCLR(nCLR[23]));  // open: nQ
  D_FlipFlop_Des d_flipflop_des_10 (
    .D(multiplexer_1_out[22]), .CLK(CLK), .Q(Salida[22]), .nPRE(nPRE[22]), .nCLR(nCLR[22]));  // open: nQ
  D_FlipFlop_Des d_flipflop_des_11 (
    .D(multiplexer_1_out[21]), .CLK(CLK), .Q(Salida[21]), .nPRE(nPRE[21]), .nCLR(nCLR[21]));  // open: nQ
  D_FlipFlop_Des d_flipflop_des_12 (
    .D(multiplexer_1_out[20]), .CLK(CLK), .Q(Salida[20]), .nPRE(nPRE[20]), .nCLR(nCLR[20]));  // open: nQ
  D_FlipFlop_Des d_flipflop_des_13 (
    .D(multiplexer_1_out[19]), .CLK(CLK), .Q(Salida[19]), .nPRE(nPRE[19]), .nCLR(nCLR[19]));  // open: nQ
  D_FlipFlop_Des d_flipflop_des_14 (
    .D(multiplexer_1_out[18]), .CLK(CLK), .Q(Salida[18]), .nPRE(nPRE[18]), .nCLR(nCLR[18]));  // open: nQ
  D_FlipFlop_Des d_flipflop_des_15 (
    .D(multiplexer_1_out[17]), .CLK(CLK), .Q(Salida[17]), .nPRE(nPRE[17]), .nCLR(nCLR[17]));  // open: nQ
  D_FlipFlop_Des d_flipflop_des_16 (
    .D(multiplexer_1_out[16]), .CLK(CLK), .Q(Salida[16]), .nPRE(nPRE[16]), .nCLR(nCLR[16]));  // open: nQ
  D_FlipFlop_Des d_flipflop_des_17 (
    .D(multiplexer_1_out[15]), .CLK(CLK), .Q(Salida[15]), .nPRE(nPRE[15]), .nCLR(nCLR[15]));  // open: nQ
  D_FlipFlop_Des d_flipflop_des_18 (
    .D(multiplexer_1_out[14]), .CLK(CLK), .Q(Salida[14]), .nPRE(nPRE[14]), .nCLR(nCLR[14]));  // open: nQ
  D_FlipFlop_Des d_flipflop_des_19 (
    .D(multiplexer_1_out[13]), .CLK(CLK), .Q(Salida[13]), .nPRE(nPRE[13]), .nCLR(nCLR[13]));  // open: nQ
  D_FlipFlop_Des d_flipflop_des_20 (
    .D(multiplexer_1_out[12]), .CLK(CLK), .Q(Salida[12]), .nPRE(nPRE[12]), .nCLR(nCLR[12]));  // open: nQ
  D_FlipFlop_Des d_flipflop_des_21 (
    .D(multiplexer_1_out[11]), .CLK(CLK), .Q(Salida[11]), .nPRE(nPRE[11]), .nCLR(nCLR[11]));  // open: nQ
  D_FlipFlop_Des d_flipflop_des_22 (
    .D(multiplexer_1_out[10]), .CLK(CLK), .Q(Salida[10]), .nPRE(nPRE[10]), .nCLR(nCLR[10]));  // open: nQ
  D_FlipFlop_Des d_flipflop_des_23 (
    .D(multiplexer_1_out[9]), .CLK(CLK), .Q(Salida[9]), .nPRE(nPRE[9]), .nCLR(nCLR[9]));  // open: nQ
  D_FlipFlop_Des d_flipflop_des_24 (
    .D(multiplexer_1_out[8]), .CLK(CLK), .Q(Salida[8]), .nPRE(nPRE[8]), .nCLR(nCLR[8]));  // open: nQ
  D_FlipFlop_Des d_flipflop_des_25 (
    .D(multiplexer_1_out[7]), .CLK(CLK), .Q(Salida[7]), .nPRE(nPRE[7]), .nCLR(nCLR[7]));  // open: nQ
  D_FlipFlop_Des d_flipflop_des_26 (
    .D(multiplexer_1_out[6]), .CLK(CLK), .Q(Salida[6]), .nPRE(nPRE[6]), .nCLR(nCLR[6]));  // open: nQ
  D_FlipFlop_Des d_flipflop_des_27 (
    .D(multiplexer_1_out[5]), .CLK(CLK), .Q(Salida[5]), .nPRE(nPRE[5]), .nCLR(nCLR[5]));  // open: nQ
  D_FlipFlop_Des d_flipflop_des_28 (
    .D(multiplexer_1_out[4]), .CLK(CLK), .Q(Salida[4]), .nPRE(nPRE[4]), .nCLR(nCLR[4]));  // open: nQ
  D_FlipFlop_Des d_flipflop_des_29 (
    .D(multiplexer_1_out[3]), .CLK(CLK), .Q(Salida[3]), .nPRE(nPRE[3]), .nCLR(nCLR[3]));  // open: nQ
  D_FlipFlop_Des d_flipflop_des_30 (
    .D(multiplexer_1_out[2]), .CLK(CLK), .Q(Salida[2]), .nPRE(nPRE[2]), .nCLR(nCLR[2]));  // open: nQ
  D_FlipFlop_Des d_flipflop_des_31 (
    .D(multiplexer_1_out[1]), .CLK(CLK), .Q(Salida[1]), .nPRE(nPRE[1]), .nCLR(nCLR[1]));  // open: nQ
  D_FlipFlop_Des d_flipflop_des_32 (
    .D(multiplexer_1_out[0]), .CLK(CLK), .Q(Salida[0]), .nPRE(nPRE[0]), .nCLR(nCLR[0]));  // open: nQ
endmodule

module Register_32_bits_Des (
  input  [31:0] nPRE,
  input  [31:0] Entrada,
  input  CLK,
  input  [31:0] nCLR,
  output [31:0] Salida
);

  D_FlipFlop_Des d_flipflop_des_1 (
    .D(Entrada[31]), .CLK(CLK), .Q(Salida[31]), .nPRE(nPRE[31]), .nCLR(nCLR[31]));  // open: nQ
  D_FlipFlop_Des d_flipflop_des_2 (
    .D(Entrada[30]), .CLK(CLK), .Q(Salida[30]), .nPRE(nPRE[30]), .nCLR(nCLR[30]));  // open: nQ
  D_FlipFlop_Des d_flipflop_des_3 (
    .D(Entrada[29]), .CLK(CLK), .Q(Salida[29]), .nPRE(nPRE[29]), .nCLR(nCLR[29]));  // open: nQ
  D_FlipFlop_Des d_flipflop_des_4 (
    .D(Entrada[28]), .CLK(CLK), .Q(Salida[28]), .nPRE(nPRE[28]), .nCLR(nCLR[28]));  // open: nQ
  D_FlipFlop_Des d_flipflop_des_5 (
    .D(Entrada[27]), .CLK(CLK), .Q(Salida[27]), .nPRE(nPRE[27]), .nCLR(nCLR[27]));  // open: nQ
  D_FlipFlop_Des d_flipflop_des_6 (
    .D(Entrada[26]), .CLK(CLK), .Q(Salida[26]), .nPRE(nPRE[26]), .nCLR(nCLR[26]));  // open: nQ
  D_FlipFlop_Des d_flipflop_des_7 (
    .D(Entrada[25]), .CLK(CLK), .Q(Salida[25]), .nPRE(nPRE[25]), .nCLR(nCLR[25]));  // open: nQ
  D_FlipFlop_Des d_flipflop_des_8 (
    .D(Entrada[24]), .CLK(CLK), .Q(Salida[24]), .nPRE(nPRE[24]), .nCLR(nCLR[24]));  // open: nQ
  D_FlipFlop_Des d_flipflop_des_9 (
    .D(Entrada[23]), .CLK(CLK), .Q(Salida[23]), .nPRE(nPRE[23]), .nCLR(nCLR[23]));  // open: nQ
  D_FlipFlop_Des d_flipflop_des_10 (
    .D(Entrada[22]), .CLK(CLK), .Q(Salida[22]), .nPRE(nPRE[22]), .nCLR(nCLR[22]));  // open: nQ
  D_FlipFlop_Des d_flipflop_des_11 (
    .D(Entrada[21]), .CLK(CLK), .Q(Salida[21]), .nPRE(nPRE[21]), .nCLR(nCLR[21]));  // open: nQ
  D_FlipFlop_Des d_flipflop_des_12 (
    .D(Entrada[20]), .CLK(CLK), .Q(Salida[20]), .nPRE(nPRE[20]), .nCLR(nCLR[20]));  // open: nQ
  D_FlipFlop_Des d_flipflop_des_13 (
    .D(Entrada[19]), .CLK(CLK), .Q(Salida[19]), .nPRE(nPRE[19]), .nCLR(nCLR[19]));  // open: nQ
  D_FlipFlop_Des d_flipflop_des_14 (
    .D(Entrada[18]), .CLK(CLK), .Q(Salida[18]), .nPRE(nPRE[18]), .nCLR(nCLR[18]));  // open: nQ
  D_FlipFlop_Des d_flipflop_des_15 (
    .D(Entrada[17]), .CLK(CLK), .Q(Salida[17]), .nPRE(nPRE[17]), .nCLR(nCLR[17]));  // open: nQ
  D_FlipFlop_Des d_flipflop_des_16 (
    .D(Entrada[16]), .CLK(CLK), .Q(Salida[16]), .nPRE(nPRE[16]), .nCLR(nCLR[16]));  // open: nQ
  D_FlipFlop_Des d_flipflop_des_17 (
    .D(Entrada[15]), .CLK(CLK), .Q(Salida[15]), .nPRE(nPRE[15]), .nCLR(nCLR[15]));  // open: nQ
  D_FlipFlop_Des d_flipflop_des_18 (
    .D(Entrada[14]), .CLK(CLK), .Q(Salida[14]), .nPRE(nPRE[14]), .nCLR(nCLR[14]));  // open: nQ
  D_FlipFlop_Des d_flipflop_des_19 (
    .D(Entrada[13]), .CLK(CLK), .Q(Salida[13]), .nPRE(nPRE[13]), .nCLR(nCLR[13]));  // open: nQ
  D_FlipFlop_Des d_flipflop_des_20 (
    .D(Entrada[12]), .CLK(CLK), .Q(Salida[12]), .nPRE(nPRE[12]), .nCLR(nCLR[12]));  // open: nQ
  D_FlipFlop_Des d_flipflop_des_21 (
    .D(Entrada[11]), .CLK(CLK), .Q(Salida[11]), .nPRE(nPRE[11]), .nCLR(nCLR[11]));  // open: nQ
  D_FlipFlop_Des d_flipflop_des_22 (
    .D(Entrada[10]), .CLK(CLK), .Q(Salida[10]), .nPRE(nPRE[10]), .nCLR(nCLR[10]));  // open: nQ
  D_FlipFlop_Des d_flipflop_des_23 (
    .D(Entrada[9]), .CLK(CLK), .Q(Salida[9]), .nPRE(nPRE[9]), .nCLR(nCLR[9]));  // open: nQ
  D_FlipFlop_Des d_flipflop_des_24 (
    .D(Entrada[8]), .CLK(CLK), .Q(Salida[8]), .nPRE(nPRE[8]), .nCLR(nCLR[8]));  // open: nQ
  D_FlipFlop_Des d_flipflop_des_25 (
    .D(Entrada[7]), .CLK(CLK), .Q(Salida[7]), .nPRE(nPRE[7]), .nCLR(nCLR[7]));  // open: nQ
  D_FlipFlop_Des d_flipflop_des_26 (
    .D(Entrada[6]), .CLK(CLK), .Q(Salida[6]), .nPRE(nPRE[6]), .nCLR(nCLR[6]));  // open: nQ
  D_FlipFlop_Des d_flipflop_des_27 (
    .D(Entrada[5]), .CLK(CLK), .Q(Salida[5]), .nPRE(nPRE[5]), .nCLR(nCLR[5]));  // open: nQ
  D_FlipFlop_Des d_flipflop_des_28 (
    .D(Entrada[4]), .CLK(CLK), .Q(Salida[4]), .nPRE(nPRE[4]), .nCLR(nCLR[4]));  // open: nQ
  D_FlipFlop_Des d_flipflop_des_29 (
    .D(Entrada[3]), .CLK(CLK), .Q(Salida[3]), .nPRE(nPRE[3]), .nCLR(nCLR[3]));  // open: nQ
  D_FlipFlop_Des d_flipflop_des_30 (
    .D(Entrada[2]), .CLK(CLK), .Q(Salida[2]), .nPRE(nPRE[2]), .nCLR(nCLR[2]));  // open: nQ
  D_FlipFlop_Des d_flipflop_des_31 (
    .D(Entrada[1]), .CLK(CLK), .Q(Salida[1]), .nPRE(nPRE[1]), .nCLR(nCLR[1]));  // open: nQ
  D_FlipFlop_Des d_flipflop_des_32 (
    .D(Entrada[0]), .CLK(CLK), .Q(Salida[0]), .nPRE(nPRE[0]), .nCLR(nCLR[0]));  // open: nQ
endmodule

module Register_8_bits_Hold___Paralel_Load (
  input  [7:0] nPRE,
  input  [7:0] Entrada,
  input  LOAD,
  input  CLK,
  input  [7:0] nCLR,
  output [7:0] Salida
);

  wire [7:0] multiplexer_1_out;

  Multiplexer #(.width(8), .enable("false")) multiplexer_1 (
    .in1(Entrada), .out(multiplexer_1_out), .sel(LOAD));  // open: in0
  D_FlipFlop_Des d_flipflop_des_1 (
    .D(multiplexer_1_out[0]), .CLK(CLK), .Q(Salida[0]), .nPRE(nPRE[0]), .nCLR(nCLR[0]));  // open: nQ
  D_FlipFlop_Des d_flipflop_des_2 (
    .D(multiplexer_1_out[1]), .CLK(CLK), .Q(Salida[1]), .nPRE(nPRE[1]), .nCLR(nCLR[1]));  // open: nQ
  D_FlipFlop_Des d_flipflop_des_3 (
    .D(multiplexer_1_out[2]), .CLK(CLK), .Q(Salida[2]), .nPRE(nPRE[2]), .nCLR(nCLR[2]));  // open: nQ
  D_FlipFlop_Des d_flipflop_des_4 (
    .D(multiplexer_1_out[3]), .CLK(CLK), .Q(Salida[3]), .nPRE(nPRE[3]), .nCLR(nCLR[3]));  // open: nQ
  D_FlipFlop_Des d_flipflop_des_5 (
    .D(multiplexer_1_out[4]), .CLK(CLK), .Q(Salida[4]), .nPRE(nPRE[4]), .nCLR(nCLR[4]));  // open: nQ
  D_FlipFlop_Des d_flipflop_des_6 (
    .D(multiplexer_1_out[5]), .CLK(CLK), .Q(Salida[5]), .nPRE(nPRE[5]), .nCLR(nCLR[5]));  // open: nQ
  D_FlipFlop_Des d_flipflop_des_7 (
    .D(multiplexer_1_out[6]), .CLK(CLK), .Q(Salida[6]), .nPRE(nPRE[6]), .nCLR(nCLR[6]));  // open: nQ
  D_FlipFlop_Des d_flipflop_des_8 (
    .D(multiplexer_1_out[7]), .CLK(CLK), .Q(Salida[7]), .nPRE(nPRE[7]), .nCLR(nCLR[7]));  // open: nQ
endmodule

module Register_4_bits_Des (
  input  [3:0] nPRE,
  input  [3:0] Entrada,
  input  CLK,
  input  [3:0] nCLR,
  output [3:0] Salida
);

  D_FlipFlop_Des d_flipflop_des_1 (
    .D(Entrada[3]), .CLK(CLK), .Q(Salida[3]), .nPRE(nPRE[3]), .nCLR(nCLR[3]));  // open: nQ
  D_FlipFlop_Des d_flipflop_des_2 (
    .D(Entrada[2]), .CLK(CLK), .Q(Salida[2]), .nPRE(nPRE[2]), .nCLR(nCLR[2]));  // open: nQ
  D_FlipFlop_Des d_flipflop_des_3 (
    .D(Entrada[1]), .CLK(CLK), .Q(Salida[1]), .nPRE(nPRE[1]), .nCLR(nCLR[1]));  // open: nQ
  D_FlipFlop_Des d_flipflop_des_4 (
    .D(Entrada[0]), .CLK(CLK), .Q(Salida[0]), .nPRE(nPRE[0]), .nCLR(nCLR[0]));  // open: nQ
endmodule

module MBR_EN (
  input  [7:0] in_1,
  input  MRB,
  input  MBRU,
  output [31:0] Salida_Signada,
  output [31:0] Salida_No_Signada
);

  assign Salida_Signada = MRB ? {{25{in_1[7]}}, in_1[6:0]} : 32'bz;  // Controlled_Buffer controlled_buffer_1
  assign Salida_No_Signada = MBRU ? {{24{1'b0}}, in_1} : 32'bz;  // Controlled_Buffer controlled_buffer_2
endmodule

module D_FlipFlop_Des (
  input  nPRE,
  input  D,
  input  CLK,
  input  nCLR,
  output Q,
  output nQ
);

  wire d_latch_1_nq, not_1_out;

  D_Latch d_latch_1 (.nPRE(nPRE), .D(D), .CLK(CLK), .nQ(d_latch_1_nq), .nCLR(nCLR));  // open: Q
  not not_1 (not_1_out, CLK);
  D_Latch d_latch_2 (.nPRE(nPRE), .D(d_latch_1_nq), .Q(Q), .CLK(not_1_out), .nQ(nQ), .nCLR(nCLR));
endmodule

module D_FlipFlop_Asc (
  input  nPRE,
  input  D,
  input  CLK,
  input  nCLR,
  output Q,
  output nQ
);

  wire d_latch_1_nq, not_1_out;

  not not_1 (not_1_out, CLK);
  D_Latch d_latch_1 (.nPRE(nPRE), .D(D), .CLK(not_1_out), .nQ(d_latch_1_nq), .nCLR(nCLR));  // open: Q
  D_Latch d_latch_2 (.nPRE(nPRE), .D(d_latch_1_nq), .Q(Q), .CLK(CLK), .nQ(nQ), .nCLR(nCLR));
endmodule

module D_Latch (
  input  nPRE,
  input  D,
  input  CLK,
  input  nCLR,
  output Q,
  output nQ
);

  wire and_1_out, and_2_out, nand_1_out, nand_2_out, not_1_out;

  not not_1 (not_1_out, D);
  nand nand_1 (nand_1_out, D, CLK);
  nand nand_2 (nand_2_out, CLK, not_1_out);
  and and_1 (and_1_out, nPRE, nand_1_out);
  and and_2 (and_2_out, nand_2_out, nCLR);
  nand nand_3 (Q, and_1_out, nQ);
  nand nand_4 (nQ, Q, and_2_out);
endmodule

module ALU_1_bit (
  input  Cin,
  input  INVA,
  input  A,
  input  ENA,
  input  B,
  input  ENB,
  input  F0,
  input  F1,
  output Suma,
  output Cout
);

  wire and_1_out, and_2_out, and_3_out, and_4_out, and_5_out, and_6_out, not_1_out, not_2_out, not_3_out,
       not_4_out, sumador_completo_alu_1_s, unidad_logica_alu_1_and, unidad_logica_alu_1_not,
       unidad_logica_alu_1_or, xor_1_out;

  and and_1 (and_1_out, A, ENA);
  and and_2 (and_2_out, B, ENB);
  not not_1 (not_1_out, F0);
  not not_2 (not_2_out, F1);
  not not_3 (not_3_out, F0);
  not not_4 (not_4_out, F1);
  xor xor_1 (xor_1_out, INVA, and_1_out);
  and and_3 (and_3_out, not_1_out, not_2_out);
  and and_4 (and_4_out, not_3_out, F1);
  and and_5 (and_5_out, F0, not_4_out);
  and and_6 (and_6_out, F0, F1);
  Unidad_Logica__ALU unidad_logica_alu_1 (
    .A(xor_1_out), .B(and_2_out), .EN1(and_3_out), .EN2(and_4_out), .EN3(and_5_out),
    .AND(unidad_logica_alu_1_and), .OR(unidad_logica_alu_1_or), .NOT(unidad_logica_alu_1_not));
  Sumador_Completo__ALU sumador_completo_alu_1 (
    .Cin(Cin), .A(and_2_out), .S(sumador_completo_alu_1_s), .B(xor_1_out), .EN(and_6_out), .Cout(Cout));
  or or_1 (Suma, unidad_logica_alu_1_and, unidad_logica_alu_1_or, unidad_logica_alu_1_not, sumador_completo_alu_1_s);
endmodule

module ALU_2_bit (
  input  Carry_in,
  input  INVA,
  input  A0,
  input  ENA,
  input  B0,
  input  ENB,
  input  F0,
  input  F1,
  input  A1,
  input  B1,
  output \output ,
  output output_2,
  output Carry_Out
);

  wire alu_1_bit_1_cout;

  ALU_1_bit alu_1_bit_1 (
    .Cin(Carry_in), .INVA(INVA), .A(A0), .Suma(\output ), .ENA(ENA), .B(B0), .ENB(ENB), .F0(F0), .F1(F1),
    .Cout(alu_1_bit_1_cout));
  ALU_1_bit alu_1_bit_2 (
    .Cin(alu_1_bit_1_cout), .INVA(INVA), .A(A1), .Suma(output_2), .ENA(ENA), .B(B1), .ENB(ENB), .F0(F0),
    .F1(F1), .Cout(Carry_Out));
endmodule

module ALU_4_bit (
  input  Carry_in,
  input  INVA,
  input  A0,
  input  ENA,
  input  B0,
  input  ENB,
  input  F0,
  input  F1,
  input  A1,
  input  B1,
  input  A2,
  input  B2,
  input  A3,
  input  B3,
  output \output ,
  output output_2,
  output output_3,
  output output_4,
  output Carry_Out
);

  wire alu_2_bit_1_carry_out;

  ALU_2_bit alu_2_bit_1 (
    .INVA(INVA), .A0(A0), .ENA(ENA), .B0(B0), .ENB(ENB), .F0(F0), .F1(F1), .A1(A1), .B1(B1),
    .\output (\output ), .output_2(output_2), .Carry_Out(alu_2_bit_1_carry_out), .Carry_in(Carry_in));
  ALU_2_bit alu_2_bit_2 (
    .INVA(INVA), .A0(A2), .ENA(ENA), .B0(B2), .ENB(ENB), .F0(F0), .F1(F1), .A1(A3), .B1(B3),
    .\output (output_3), .output_2(output_4), .Carry_Out(Carry_Out), .Carry_in(alu_2_bit_1_carry_out));
endmodule

// ALU 8 bits
module ALU_8_bit (
  input  Carry_in,
  input  INVA,
  input  A0,
  input  ENA,
  input  B0,
  input  ENB,
  input  F0,
  input  F1,
  input  A1,
  input  B1,
  input  A2,
  input  B2,
  input  A3,
  input  B3,
  input  A4,
  input  B4,
  input  A5,
  input  B5,
  input  A6,
  input  B6,
  input  A7,
  input  B7,
  output \output ,
  output output_2,
  output output_3,
  output output_4,
  output output_5,
  output output_6,
  output output_7,
  output output_8,
  output Carry_Out
);

  wire alu_4_bit_1_carry_out;

  ALU_4_bit alu_4_bit_1 (
    .INVA(INVA), .A0(A0), .ENA(ENA), .B0(B0), .ENB(ENB), .F0(F0), .F1(F1), .A1(A1), .B1(B1), .A2(A2),
    .B2(B2), .A3(A3), .B3(B3), .\output (\output ), .output_2(output_2), .output_3(output_3),
    .output_4(output_4), .Carry_Out(alu_4_bit_1_carry_out), .Carry_in(Carry_in));
  ALU_4_bit alu_4_bit_2 (
    .INVA(INVA), .A0(A4), .ENA(ENA), .B0(B4), .ENB(ENB), .F0(F0), .F1(F1), .A1(A5), .B1(B5), .A2(A6),
    .B2(B6), .A3(A7), .B3(B7), .\output (output_5), .output_2(output_6), .output_3(output_7),
    .output_4(output_8), .Carry_Out(Carry_Out), .Carry_in(alu_4_bit_1_carry_out));
endmodule

module ALU_16_bit (
  input  Carry_in,
  input  INVA,
  input  A0,
  input  ENA,
  input  B0,
  input  ENB,
  input  F0,
  input  F1,
  input  A1,
  input  B1,
  input  A2,
  input  B2,
  input  A3,
  input  B3,
  input  A4,
  input  B4,
  input  A5,
  input  B5,
  input  A6,
  input  B6,
  input  A7,
  input  B7,
  input  A8,
  input  B8,
  input  A9,
  input  B9,
  input  A10,
  input  B10,
  input  A11,
  input  B11,
  input  A12,
  input  B12,
  input  A13,
  input  B13,
  input  A14,
  input  B14,
  input  A15,
  input  B15,
  output \output ,
  output output_2,
  output output_3,
  output output_4,
  output output_5,
  output output_6,
  output output_7,
  output output_8,
  output output_9,
  output output_10,
  output output_11,
  output output_12,
  output output_13,
  output output_14,
  output output_15,
  output output_16,
  output Carry_Out
);

  wire alu_8_bit_1_carry_out;

  ALU_8_bit alu_8_bit_1 (
    .INVA(INVA), .A0(A0), .ENA(ENA), .B0(B0), .ENB(ENB), .F0(F0), .F1(F1), .A1(A1), .B1(B1), .A2(A2),
    .B2(B2), .A3(A3), .B3(B3), .A4(A4), .B4(B4), .A5(A5), .B5(B5), .A6(A6), .B6(B6), .A7(A7), .B7(B7),
    .\output (\output ), .output_2(output_2), .output_3(output_3), .output_4(output_4), .output_5(output_5),
    .output_6(output_6), .output_7(output_7), .output_8(output_8), .Carry_Out(alu_8_bit_1_carry_out),
    .Carry_in(Carry_in));
  ALU_8_bit alu_8_bit_2 (
    .INVA(INVA), .A0(A8), .ENA(ENA), .B0(B8), .ENB(ENB), .F0(F0), .F1(F1), .A1(A9), .B1(B9), .A2(A10),
    .B2(B10), .A3(A11), .B3(B11), .A4(A12), .B4(B12), .A5(A13), .B5(B13), .A6(A14), .B6(B14), .A7(A15),
    .B7(B15), .\output (output_9), .output_2(output_10), .output_3(output_11), .output_4(output_12),
    .output_5(output_13), .output_6(output_14), .output_7(output_15), .output_8(output_16),
    .Carry_Out(Carry_Out), .Carry_in(alu_8_bit_1_carry_out));
endmodule

// ALU 32 bits
module ALU_32_bit (
  input  Carry_in,
  input  INVA,
  input  A0,
  input  ENA,
  input  B0,
  input  ENB,
  input  F0,
  input  F1,
  input  A1,
  input  B1,
  input  A2,
  input  B2,
  input  A3,
  input  B3,
  input  A4,
  input  B4,
  input  A5,
  input  B5,
  input  A6,
  input  B6,
  input  A7,
  input  B7,
  input  A8,
  input  B8,
  input  A9,
  input  B9,
  input  A10,
  input  B10,
  input  A11,
  input  B11,
  input  A12,
  input  B12,
  input  A13,
  input  B13,
  input  A14,
  input  B14,
  input  A15,
  input  B15,
  input  A16,
  input  B16,
  input  A17,
  input  B17,
  input  A18,
  input  B18,
  input  A19,
  input  B19,
  input  A20,
  input  B20,
  input  A21,
  input  B21,
  input  A22,
  input  B22,
  input  A23,
  input  B23,
  input  A24,
  input  B24,
  input  A25,
  input  B25,
  input  A26,
  input  B26,
  input  A27,
  input  B27,
  input  A28,
  input  B28,
  input  A29,
  input  B29,
  input  A30,
  input  B30,
  input  A31,
  input  B31,
  output \output ,
  output output_2,
  output output_3,
  output output_4,
  output output_5,
  output output_6,
  output output_7,
  output output_8,
  output output_9,
  output output_10,
  output output_11,
  output output_12,
  output output_13,
  output output_14,
  output output_15,
  output output_16,
  output output_17,
  output output_18,
  output output_19,
  output output_20,
  output output_21,
  output output_22,
  output output_23,
  output output_24,
  output output_25,
  output output_26,
  output output_27,
  output output_28,
  output output_29,
  output output_30,
  output output_31,
  output output_32,
  output Carry_Out
);

  wire alu_16_bit_1_carry_out;

  ALU_16_bit alu_16_bit_1 (
    .INVA(INVA), .A0(A0), .ENA(ENA), .B0(B0), .ENB(ENB), .F0(F0), .F1(F1), .A1(A1), .B1(B1), .A2(A2),
    .B2(B2), .A3(A3), .B3(B3), .A4(A4), .B4(B4), .A5(A5), .B5(B5), .A6(A6), .B6(B6), .A7(A7), .B7(B7),
    .A8(A8), .B8(B8), .A9(A9), .B9(B9), .A10(A10), .B10(B10), .A11(A11), .B11(B11), .A12(A12), .B12(B12),
    .A13(A13), .B13(B13), .A14(A14), .B14(B14), .A15(A15), .B15(B15), .output_2(\output ),
    .output_3(output_3), .output_4(output_4), .output_5(output_5), .output_6(output_6), .output_7(output_7),
    .output_8(output_8), .output_9(output_9), .output_10(output_10), .output_11(output_11),
    .output_12(output_12), .output_13(output_13), .output_14(output_14), .output_15(output_15),
    .output_16(output_16), .Carry_Out(alu_16_bit_1_carry_out), .Carry_in(Carry_in), .\output (output_2));
  ALU_16_bit alu_16_bit_2 (
    .INVA(INVA), .A0(A16), .ENA(ENA), .B0(B16), .ENB(ENB), .F0(F0), .F1(F1), .A1(A17), .B1(B17), .A2(A18),
    .B2(B18), .A3(A19), .B3(B19), .A4(A20), .B4(B20), .A5(A21), .B5(B21), .A6(A22), .B6(B22), .A7(A23),
    .B7(B23), .A8(A24), .B8(B24), .A9(A25), .B9(B25), .A10(A26), .B10(B26), .A11(A27), .B11(B27), .A12(A28),
    .B12(B28), .A13(A29), .B13(B29), .A14(A30), .B14(B30), .A15(A31), .B15(B31), .output_2(output_17),
    .output_3(output_19), .output_4(output_20), .output_5(output_21), .output_6(output_22),
    .output_7(output_23), .output_8(output_24), .output_9(output_25), .output_10(output_26),
    .output_11(output_27), .output_12(output_28), .output_13(output_29), .output_14(output_30),
    .output_15(output_31), .output_16(output_32), .Carry_Out(Carry_Out), .Carry_in(alu_16_bit_1_carry_out),
    .\output (output_18));
endmodule

module Unidad_Logica__ALU (
  input  A,
  input  B,
  input  EN1,
  input  EN2,
  input  EN3,
  output AND,
  output OR,
  output NOT
);

  wire and_1_out, not_1_out, or_1_out;

  and and_1 (and_1_out, A, B);
  or or_1 (or_1_out, A, B);
  not not_1 (not_1_out, B);
  and and_2 (AND, and_1_out, EN1);
  and and_3 (OR, or_1_out, EN2);
  and and_4 (NOT, not_1_out, EN3);

  // Notes on the sheet:
  //   AB
  //   A+B
  //   /B
endmodule

module Sumador_Completo__ALU (
  input  Cin,
  input  A,
  input  B,
  input  EN,
  output S,
  output Cout
);

  wire and_1_out, and_2_out, and_3_out, and_4_out, xor_1_out;

  and and_1 (and_1_out, A, EN);
  and and_2 (and_2_out, B, EN);
  and and_3 (and_3_out, and_1_out, and_2_out);
  xor xor_1 (xor_1_out, and_1_out, and_2_out);
  or or_1 (Cout, and_3_out, and_4_out);
  and and_4 (and_4_out, xor_1_out, Cin);
  xor xor_2 (S, Cin, xor_1_out);
endmodule

module Desplazador (
  input  [31:0] Entrada,
  input  C,
  output [31:0] Salida
);

  wire and_1_out, and_3_out, and_4_out, and_5_out, and_6_out, and_7_out, and_8_out, and_9_out, and_10_out,
       and_11_out, and_12_out, and_13_out, and_14_out, and_15_out, and_16_out, and_17_out, and_18_out,
       and_19_out, and_20_out, and_21_out, and_22_out, and_23_out, and_24_out, and_25_out, and_26_out,
       and_27_out, and_28_out, and_29_out, and_30_out, and_31_out, and_32_out, and_33_out, and_34_out,
       and_35_out, and_36_out, and_37_out, and_38_out, and_39_out, and_40_out, and_41_out, and_42_out,
       and_43_out, and_44_out, and_45_out, and_46_out, and_47_out, and_48_out, and_49_out, and_50_out,
       and_51_out, and_52_out, and_53_out, and_54_out, and_55_out, and_56_out, and_57_out, and_58_out,
       and_59_out, and_60_out, and_62_out, not_1_out;

  and and_1 (and_1_out, Entrada[31], not_1_out);
  and and_2 (Salida[31], C, Entrada[30]);
  and and_3 (and_3_out, Entrada[30], not_1_out);
  or or_1 (Salida[30], and_1_out, and_4_out);
  and and_4 (and_4_out, C, Entrada[29]);
  and and_5 (and_5_out, Entrada[29], not_1_out);
  or or_2 (Salida[29], and_3_out, and_6_out);
  and and_6 (and_6_out, C, Entrada[28]);
  or or_3 (Salida[28], and_5_out, and_9_out);
  and and_7 (and_7_out, Entrada[28], not_1_out);
  and and_8 (and_8_out, Entrada[27], not_1_out);
  and and_9 (and_9_out, C, Entrada[27]);
  or or_4 (Salida[27], and_7_out, and_10_out);
  and and_10 (and_10_out, C, Entrada[26]);
  and and_11 (and_11_out, Entrada[26], not_1_out);
  or or_5 (Salida[26], and_8_out, and_12_out);
  and and_12 (and_12_out, C, Entrada[25]);
  and and_13 (and_13_out, Entrada[25], not_1_out);
  or or_6 (Salida[25], and_11_out, and_14_out);
  and and_14 (and_14_out, C, Entrada[24]);
  or or_7 (Salida[24], and_13_out, and_17_out);
  and and_15 (and_15_out, Entrada[24], not_1_out);
  and and_16 (and_16_out, Entrada[23], not_1_out);
  and and_17 (and_17_out, C, Entrada[23]);
  or or_8 (Salida[23], and_15_out, and_18_out);
  and and_18 (and_18_out, C, Entrada[22]);
  and and_19 (and_19_out, Entrada[22], not_1_out);
  or or_9 (Salida[22], and_16_out, and_20_out);
  and and_20 (and_20_out, C, Entrada[21]);
  and and_21 (and_21_out, Entrada[21], not_1_out);
  or or_10 (Salida[21], and_19_out, and_22_out);
  and and_22 (and_22_out, C, Entrada[20]);
  or or_11 (Salida[20], and_21_out, and_25_out);
  and and_23 (and_23_out, Entrada[20], not_1_out);
  and and_24 (and_24_out, Entrada[19], not_1_out);
  and and_25 (and_25_out, C, Entrada[19]);
  or or_12 (Salida[19], and_23_out, and_26_out);
  and and_26 (and_26_out, C, Entrada[18]);
  and and_27 (and_27_out, Entrada[18], not_1_out);
  or or_13 (Salida[18], and_24_out, and_28_out);
  and and_28 (and_28_out, C, Entrada[17]);
  or or_14 (Salida[17], and_27_out, and_30_out);
  and and_29 (and_29_out, Entrada[17], not_1_out);
  and and_30 (and_30_out, C, Entrada[16]);
  or or_15 (Salida[16], and_29_out, and_32_out);
  and and_31 (and_31_out, Entrada[16], not_1_out);
  and and_32 (and_32_out, C, Entrada[15]);
  and and_33 (and_33_out, Entrada[15], not_1_out);
  or or_16 (Salida[15], and_31_out, and_34_out);
  and and_34 (and_34_out, C, Entrada[14]);
  and and_35 (and_35_out, Entrada[14], not_1_out);
  or or_17 (Salida[14], and_33_out, and_36_out);
  and and_36 (and_36_out, C, Entrada[13]);
  or or_18 (Salida[13], and_35_out, and_38_out);
  and and_37 (and_37_out, Entrada[13], not_1_out);
  and and_38 (and_38_out, C, Entrada[12]);
  or or_19 (Salida[12], and_37_out, and_40_out);
  and and_39 (and_39_out, Entrada[12], not_1_out);
  and and_40 (and_40_out, C, Entrada[11]);
  and and_41 (and_41_out, Entrada[11], not_1_out);
  or or_20 (Salida[11], and_39_out, and_42_out);
  and and_42 (and_42_out, C, Entrada[10]);
  and and_43 (and_43_out, Entrada[10], not_1_out);
  or or_21 (Salida[10], and_41_out, and_44_out);
  and and_44 (and_44_out, C, Entrada[9]);
  or or_22 (Salida[9], and_43_out, and_46_out);
  and and_45 (and_45_out, Entrada[9], not_1_out);
  and and_46 (and_46_out, C, Entrada[8]);
  or or_23 (Salida[8], and_45_out, and_49_out);
  and and_47 (and_47_out, Entrada[8], not_1_out);
  and and_48 (and_48_out, Entrada[7], not_1_out);
  and and_49 (and_49_out, C, Entrada[7]);
  or or_24 (Salida[7], and_47_out, and_50_out);
  and and_50 (and_50_out, C, Entrada[6]);
  and and_51 (and_51_out, Entrada[6], not_1_out);
  or or_25 (Salida[6], and_48_out, and_52_out);
  and and_52 (and_52_out, C, Entrada[5]);
  or or_26 (Salida[5], and_51_out, and_55_out);
  and and_53 (and_53_out, Entrada[5], not_1_out);
  and and_54 (and_54_out, Entrada[4], not_1_out);
  and and_55 (and_55_out, C, Entrada[4]);
  or or_27 (Salida[4], and_53_out, and_56_out);
  and and_56 (and_56_out, C, Entrada[3]);
  and and_57 (and_57_out, Entrada[3], not_1_out);
  or or_28 (Salida[3], and_54_out, and_58_out);
  and and_58 (and_58_out, C, Entrada[2]);
  and and_59 (and_59_out, Entrada[2], not_1_out);
  or or_29 (Salida[2], and_57_out, and_60_out);
  and and_60 (and_60_out, C, Entrada[1]);
  or or_30 (Salida[1], and_59_out, and_62_out);
  and and_61 (Salida[0], Entrada[1], not_1_out);
  and and_62 (and_62_out, C, Entrada[0]);
  not not_1 (not_1_out, C);

  // Notes on the sheet:
  //   D31
  //   S31
  //   S0
  //   D0
endmodule

module Shifter (
  input  [31:0] Entrada,
  input  SRA1,
  input  SLL8,
  output [31:0] Salida
);

  wire and_1_out, and_2_out, and_3_out, and_4_out, not_1_out, not_2_out;
  wire [31:0] shifter_1_out, shifter_2_out;

  not not_1 (not_1_out, SRA1);
  not not_2 (not_2_out, SLL8);
  and and_1 (and_1_out, not_1_out, not_2_out);
  and and_2 (and_2_out, not_1_out, SLL8);
  and and_3 (and_3_out, SRA1, not_2_out);
  and and_4 (and_4_out, SRA1, SLL8);
  assign Salida = and_1_out ? Entrada : 32'bz;  // Controlled_Buffer controlled_buffer_1
  assign Salida = and_4_out ? Entrada : 32'bz;  // Controlled_Buffer controlled_buffer_2
  Shifter_part #(.width(32)) shifter_1 (.in(Entrada), .\dist (5'b01000), .out(shifter_1_out));
  Shifter_part #(.width(32), .shift("ar")) shifter_2 (.in(Entrada), .\dist (5'b01000), .out(shifter_2_out));
  assign Salida = and_2_out ? shifter_1_out : 32'bz;  // Controlled_Buffer controlled_buffer_3
  assign Salida = and_3_out ? shifter_2_out : 32'bz;  // Controlled_Buffer controlled_buffer_4

  // Notes on the sheet:
  //   Logical Left
  //   Arithmetic Right
endmodule
